// Logisim project Examples.circ as structural Verilog: 1 circuit, main circuit main
module main (
  input  in_1,
  input  [3:0] in_2
);

  wire clock_1_out, d_ff_1_q;
  wire [3:0] register_1_q;

  Clock clock_1 (.out(clock_1_out));
  D_Flip_Flop d_ff_1 (.clk(clock_1_out), .D(in_1), .Q(d_ff_1_q), .preset(1'b0), .en(1'b1), .reset(1'b0));  // open: Qn
  Register #(.width(4)) register_1 (.D(in_2), .en(1'b1), .Q(register_1_q), .clk(clock_1_out), .clr(1'b0));
  // Probe on d_ff_1_q
  // Probe on register_1_q

  // Notes on the sheet:
  //   Clock
  //   Flip-Flop
  //   4-bit Register
endmodule
