// Logisim project Project3.circ as structural Verilog: 1 circuit, main circuit main
module main (
  input  [1:0] in_1
);

  wire and_1_out, and_2_out, and_3_out, and_4_out, and_5_out, and_6_out, and_7_out, and_8_out, and_9_out,
       and_10_out, clock_1_out, not_1_out, not_2_out, not_3_out, not_4_out, or_1_out, or_2_out, or_3_out,
       or_4_out, or_5_out;
  wire [3:0] adder_1_out, divider_1_rem, register_1_q;

  Clock clock_1 (.out(clock_1_out));
  Adder #(.width(4)) adder_1 (.a(register_1_q), .b({2'b00, in_1}), .out(adder_1_out));  // open: cin, cout
  not not_1 (not_1_out, register_1_q[3]);
  Divider #(.width(4)) divider_1 (.a(adder_1_out), .b(4'b1010), .rem(divider_1_rem));  // open: out, upper
  not not_2 (not_2_out, register_1_q[1]);
  not not_3 (not_3_out, register_1_q[0]);
  not not_4 (not_4_out, register_1_q[2]);
  Register #(.width(4)) register_1 (.D(divider_1_rem), .Q(register_1_q), .clk(clock_1_out), .clr(1'b0));  // open: en
  and and_1 (and_1_out, register_1_q[1], register_1_q[2]);
  and and_2 (and_2_out, not_3_out, not_2_out, not_4_out);
  and and_3 (and_3_out, not_4_out, not_2_out);
  and and_4 (and_4_out, register_1_q[2], register_1_q[1], register_1_q[0]);
  and and_5 (and_5_out, not_4_out, not_2_out);
  and and_6 (and_6_out, not_4_out, not_3_out);
  and and_7 (and_7_out, not_1_out, not_4_out);
  and and_8 (and_8_out, register_1_q[3], register_1_q[0]);
  and and_9 (and_9_out, not_1_out, not_4_out);
  and and_10 (and_10_out, not_1_out, not_2_out, not_3_out);
  Hex_Digit_Display hex_digit_display_1 (.value(register_1_q));  // open: dp
  LED led_1 (.in(or_1_out));
  LED led_2 (.in(or_3_out));
  LED led_3 (.in(or_2_out));
  or or_1 (or_1_out, and_1_out, register_1_q[3], and_2_out);
  or or_2 (or_2_out, and_3_out, and_4_out);
  or or_3 (or_3_out, and_5_out, and_6_out);
  or or_4 (or_4_out, and_7_out, and_8_out);
  or or_5 (or_5_out, and_9_out, and_10_out);
  LED led_4 (.in(or_4_out));
  LED led_5 (.in(or_5_out));

  // Notes on the sheet:
  //   Peter Schaefer
  //   October 25th, 2023
  //   A'
  //   B'
  //   Counter
  //   B
  //   A
  //   D
  //   D'
  //   C'
  //   C
  //   Decoder
  //   Left
  //   Center Left
  //   Center
  //   Center Right
  //   Right
endmodule
