// Logisim project primes.circ as structural Verilog: 1 circuit, main circuit main
module main (
  input  [2:0] NUM_1,
  input  [2:0] NUM_2
);

  wire and_1_out, and_2_out, and_3_out, nor_1_out, nor_2_out, not_1_out, not_2_out, not_3_out, not_4_out,
       not_5_out, xor_1_out, xor_2_out;
  wire [3:0] adder_1_out, bit_extender_1_out, bit_extender_2_out, divider_1_rem;

  assign bit_extender_1_out = {{1{1'b0}}, NUM_1};  // Bit_Extender bit_extender_1
  assign bit_extender_2_out = {{1{1'b0}}, NUM_2};  // Bit_Extender bit_extender_2
  Hex_Digit_Display hex_digit_display_1 (.value(adder_1_out));  // open: dp
  Adder #(.width(4)) adder_1 (.a(bit_extender_1_out), .b(bit_extender_2_out), .out(adder_1_out));  // open: cin, cout
  Divider #(.width(4)) divider_1 (.a(adder_1_out), .b(4'b0011), .rem(divider_1_rem));  // open: out, upper
  not not_1 (not_1_out, adder_1_out[1]);
  not not_2 (not_2_out, adder_1_out[0]);
  not not_3 (not_3_out, adder_1_out[2]);
  not not_4 (not_4_out, adder_1_out[3]);
  not not_5 (not_5_out, adder_1_out[0]);
  and and_1 (and_1_out, adder_1_out[0], not_1_out, not_3_out, not_4_out);
  and and_2 (and_2_out, not_2_out, adder_1_out[1], not_3_out, not_4_out);
  and and_3 (and_3_out, adder_1_out[0], adder_1_out[1], not_3_out, not_4_out);
  nor nor_1 (nor_1_out, divider_1_rem[0], divider_1_rem[1], divider_1_rem[2], divider_1_rem[3]);
  xor xor_1 (xor_1_out, and_2_out, not_5_out);
  xor xor_2 (xor_2_out, and_3_out, nor_1_out);
  nor nor_2 (nor_2_out, and_1_out, xor_1_out, xor_2_out);
  LED PRIME (.in(nor_2_out));

  // Notes on the sheet:
  //   Primes Circuit
  //   Decoder
  //   Divider
  //   Final Logic
  //   Peter Schaefer
  //   September 20, 2023
endmodule
